# Fritzing sketch wiring (saved by Fritzing 0.9.9b)
breadboards: 1

parts:
  J1 = STM32 Nucleo boards
  HC-SR04_Sensor_1 = HC-SR04 Ultrasonic Distance Sensor
  Componente1 = HC-SR501 Body Sensor Module
  LED1 = smd LED [color="Red (633nm)" package="0805 [SMD]"]
  R1 = Resistor [tolerance=±5% resistance=220 package="1206 [SMD]"]
  SM1 = 28BYJ-48 Stepper Motor [part_number=28BYJ-48]
  Driver1 = 28BYJ-48 Driver Module [part_number=ULN2003 package=THT]

nets:
  N1: J1.A0, Componente1.OUT
  N2: J1.D8, HC-SR04_Sensor_1.TRIG
  N3: J1.D9_PWM, R1.Pin_1
  N4: J1.D3_PWM, Driver1.IN1
  N5: J1.D4, Driver1.IN2
  N6: J1.D5_PWM, Driver1.IN3
  N7: J1.D6_PWM, Driver1.IN4
  N8: J1.D7, HC-SR04_Sensor_1.ECHO
  VCC: J1.5V, HC-SR04_Sensor_1.VCC, Componente1.VCC, Driver1.Vmotor
  GND: J1.GND, HC-SR04_Sensor_1.GND, Componente1.GND, LED1.cathode, Driver1.GND
  N9: LED1.anode, R1.Pin_0
  N10: SM1.blue-pin, Driver1.blue-pin
  N11: SM1.pink-pin, Driver1.pink-pin
  N12: SM1.yellow-pin, Driver1.yellow-pin
  N13: SM1.orange-pin, Driver1.orange-pin
  N14: SM1.red-pin, Driver1.red-pin

custom parts:
  HC-SR501 Body Sensor Module: Pyroelectric Infrared PIR Motion Sensor Detector Module
  28BYJ-48 Stepper Motor: Unipolar Stepper Motor 28BYJ-48 Top coil - pink & orange Bottom coil - blue & yellow Common rail - red Connector pins: blue - pink - yellow - orange - red
  28BYJ-48 Driver Module: ULN2003 Driver Module for the 28BYJ-48 Unipolar Stepper Motor LED A - Blue wire - Bottom coil left LED B - Pink wire - Top coil left LED C - Yellow wire - Bottom coil right LED D - Orange wire - Top coil right Common rail - red Connector pins: blue - pink - yellow - orange - red Control pins - IN1 to IN4 Power pins - GND & Vmotor (5-12V) On/Off jumper (if removed, power to motor is cut).
